# Fritzing sketch breadboard (saved by Fritzing 0.9.3b)
circuit board: 9.07541cm x 6.27162cm
breadboards: 1

parts:
  WeMos_D1_Mini1 = WeMos D1 Mini
  Power_plug1 = Power plug
  S1 = H-Bridge with L298N
  M1 = DC Motor
  LED1 = LED - 5mm [color="Red (633nm)" package="5 mm [THT]"]
  LED2 = LED - 5mm [color="Orange (620nm)" package="5 mm [THT]"]
  LED3 = LED - 5mm [color="Yellow (595nm)" package="5 mm [THT]"]
  S2 = Momentary Switch [package=ksa_sealed_tac_switch]
  S3 = Momentary Switch [package=ksa_sealed_tac_switch]
  J2 = screw terminal, 2 pins
  R1 = Resistor [tolerance=±5% resistance=220 package=THT]
  R2 = Resistor [tolerance=±5% resistance=220 package=THT]
  VCC1 = Battery
  U1 = Module 4 Relais 5V [package="Module 4 Relais 5V"]
  LLC1 = Logic Level Converter [package="Breakout board"]
  J1 = Screw terminal - 2 pins [package=THT]

nets:
  N1: WeMos_D1_Mini1.D0, S3.4
  N2: WeMos_D1_Mini1.D1, S1.IN1
  N3: WeMos_D1_Mini1.D2, S1.IN2
  N4: WeMos_D1_Mini1.D4, LLC1.LV3
  N5: WeMos_D1_Mini1.D5, LLC1.LV1
  N6: WeMos_D1_Mini1.D6, LLC1.LV4
  GND: WeMos_D1_Mini1.G, Power_plug1.GND, S1.GND, LED1.anode, J2.pin1, J2.pin2, R1.Pin_1, R2.Pin_1, U1.GND, LLC1.L-GND, LLC1.H-GND
  N7: WeMos_D1_Mini1.RX, S2.4
  VCC: Power_plug1.VCC, S1.12V, U1.K1-Com
  5V: S1.5V, S2.1, S3.1, U1.VCC, LLC1.HV, J1.pin1, J1.pin2
  N8: S1.M1-01, M1.pin_2
  N9: S1.M1-02, M1.pin_1
  N10: LED1.cathode, U1.K1-NF
  N11: LED2.cathode, U1.K2-NF
  N12: LED3.cathode, U1.K3-NF
  N13: S2.3, R2.Pin_0
  N14: S3.3, R1.Pin_0
  N15: VCC1.+, U1.K2-Com, U1.K3-Com
  N16: U1.IN2, LLC1.HV3
  N17: U1.IN3, LLC1.HV1
  N18: U1.IN4, LLC1.HV4

custom parts:
  WeMos D1 Mini: The D1 mini is a mini wifi board based on ESP-8266EX.
  H-Bridge with L298N: h-bridge
  Module 4 Relais 5V: Module 4 Relais 5V 4x SPD-06VDC-SD-C
  Logic Level Converter: 5V to/from 3.3V logic level converter
