# Fritzing sketch pcb (saved by Fritzing 0.9.3b)
circuit board: 11.6888cm x 7.40049cm
breadboards: 1

parts:
  S1 = H-Bridge with L298N
  S3 = Momentary Switch [package=ksa_sealed_tac_switch]  # not connected
  R2 = Resistor [tolerance=±5% resistance=220 package=THT]
  U1 = Module 4 Relais 5V [package="Module 4 Relais 5V"]  # not connected
  LLC1 = Logic Level Converter [package="Breakout board"]
  J2_-_btn2 = screw terminal, 2 pins
  J3_-_motor = screw terminal, 2 pins
  J4 = screw terminal, 6 pins
  J1_-_power = screw terminal, 2 pins
  J5_-_btn1 = screw terminal, 2 pins
  R1 = Resistor [tolerance=±5% resistance=220 package=THT]
  WeMos_D1_Mini1 = WeMos D1 Mini
  S2 = Momentary Switch [package=ksa_sealed_tac_switch]

nets:
  N1: S1.IN2, S1.M1-02, S1.M2-01, S1.M2-02, S1.ENA-5V, S1.ENB-5V
  N2: R2.Pin_0, J2_-_btn2.pin1, WeMos_D1_Mini1.D7
  N3: R2.Pin_1, LLC1.L-GND, LLC1.H-GND, J4.pin3, J1_-_power.pin1, R1.Pin_1, WeMos_D1_Mini1.G
  N4: LLC1.LV1, WeMos_D1_Mini1.D5
  N5: LLC1.LV2, WeMos_D1_Mini1.D6
  N6: LLC1.LV, WeMos_D1_Mini1.3V3
  N7: LLC1.LV3, WeMos_D1_Mini1.D4
  N8: LLC1.HV4, J4.pin1
  N9: LLC1.HV3, J4.pin2
  N10: LLC1.HV, J2_-_btn2.pin2, J4.pin4, J1_-_power.pin2, J5_-_btn1.pin2
  N11: LLC1.HV2, J4.pin5
  N12: LLC1.HV1, J4.pin6
  N13: J3_-_motor.pin1, WeMos_D1_Mini1.D2
  N14: J3_-_motor.pin2, WeMos_D1_Mini1.D1
  N15: J5_-_btn1.pin1, R1.Pin_0, WeMos_D1_Mini1.D0
  N16: S2.2, S2.4

custom parts:
  H-Bridge with L298N: h-bridge
  Module 4 Relais 5V: Module 4 Relais 5V 4x SPD-06VDC-SD-C
  Logic Level Converter: 5V to/from 3.3V logic level converter
